// Logisim project ex4.circ as structural Verilog: 1 circuit, main circuit Split
module Split (
  input  [7:0] In1,
  output Out1,
  output [7:0] Out2
);

  Adder adder_1 (.a(In1), .b(8'h80), .out(Out2));  // open: cin, cout
  and and_1 (Out1, In1[0], In1[7]);

  // Notes on the sheet:
  //   PUT CIRCUITRY HERE
endmodule
